# Fritzing sketch Schema Arduino (saved by Fritzing 0.9.3b)
breadboards: 1

parts:
  Arduino = Arduino Uno (Rev3)
  Modul_bluetooth = Bluetooth HC-05 Macho
  Modul_RFID = RFID USB Reader
  LED_R = LTE-302 [package=lte-302]
  LED_V = LTE-302 [package=lte-302]
  Antena_RFID = Antenna
  Baterie_9v = BC9VPC [package=bc9vpc]

nets:
  N1: Arduino.D8, LED_V.A
  N2: Arduino.D10_PWM/SS, Modul_RFID.TX-O-RS232
  N3: Arduino.D11_PWM/MOSI, Modul_RFID.TX-O
  GND: Arduino.GND, Modul_bluetooth.GND, Modul_RFID.GND, LED_R.C, LED_V.C, Baterie_9v.V-
  N4: Arduino.D0/RX, Modul_bluetooth.RXD
  N5: Arduino.D1/TX, Modul_bluetooth.TXD
  N6: Arduino.D7, LED_R.A
  VCC: Arduino.5V, Modul_bluetooth.VCC, Modul_RFID.VCC
  N7: Arduino.VIN, Baterie_9v.V+
  N8: Modul_RFID.ANT1, Antena_RFID.antenna_lead
